# Fritzing sketch diagram (saved by Fritzing 1.0.1rc)
breadboards: 1

parts:
  Mod1 = Raspberry Pi Pico
  U1 = WS2812 RGB LED strip
  C1 = Electrolytic Capacitor [capacitance=1000µF voltage=35V package="300 mil [THT, electrolytic]"]
  Power_plug1 = Power plug
  Part1 = HC-SR501 Body Sensor Module
  Part2 = HC-SR501 Body Sensor Module  # not connected

nets:
  GND: Mod1.pin_3, Mod1.pin_9, Mod1.pin_13, Mod1.pin_18, Mod1.pin_23, Mod1.pin_28, Mod1.pin_33, Mod1.pin_42, C1.-, Power_plug1.GND, Part1.GND
  N1: Mod1.pin_6, Mod1.pin_14
  VCC: Mod1.pin_12, Mod1.pin_27, U1.VCC, C1.+, Power_plug1.VCC, Part1.VCC

custom parts:
  Raspberry Pi Pico: Raspberry Pi Pico. Based around the RP2040 microcontroller the Pico is a low cost microcontroller device bringing Raspberry Pi quality, cost, and easy of use to the microcontroller space. Jan 2021, Split part in to two versions: tht (this one) and SMD. This one will drill holes for a .1 in header in pcb to allow plugging in the module as well as providing pads to solder the module to the top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
  WS2812 RGB LED strip: WS2812 strip
  HC-SR501 Body Sensor Module: Pyroelectric Infrared PIR Motion Sensor Detector Module
